# Fritzing sketch Circuito (saved by Fritzing 0.9.3b)
breadboards: 1

parts:
  MH-ET_LIVE_ESP32_DEVKIT1 = MH-ET LIVE ESP32 DEVKIT 38 pins
  M2 = DC Motor
  M3 = DC Motor
  hc-sr1 = hc-sr04
  hc-sr2 = hc-sr04
  hc-sr3 = hc-sr04
  hc-sr4 = hc-sr04
  Q1 = TRANSISTOR_PNP [package=to-92]
  VCC1 = 4 x AAA Battery Mount
  J1 = Basic Servo

nets:
  N1: MH-ET_LIVE_ESP32_DEVKIT1.IO26, hc-sr4.Echo
  N2: MH-ET_LIVE_ESP32_DEVKIT1.IO27, hc-sr4.Trig
  N3: MH-ET_LIVE_ESP32_DEVKIT1.IO14, hc-sr3.Echo
  N4: MH-ET_LIVE_ESP32_DEVKIT1.IO12, hc-sr3.Trig
  N5: MH-ET_LIVE_ESP32_DEVKIT1.GND, hc-sr1.Echo
  N6: MH-ET_LIVE_ESP32_DEVKIT1.IO13, hc-sr1.Trig
  N7: MH-ET_LIVE_ESP32_DEVKIT1.SD2, hc-sr2.Echo
  N8: MH-ET_LIVE_ESP32_DEVKIT1.SD3, hc-sr2.Trig
  N9: MH-ET_LIVE_ESP32_DEVKIT1.IO0, J1.pulse
  N10: MH-ET_LIVE_ESP32_DEVKIT1.IO15, M2.pin_2
  N11: MH-ET_LIVE_ESP32_DEVKIT1.SD1, M3.pin_2
  N12: MH-ET_LIVE_ESP32_DEVKIT1.SCK, Q1.B
  GND: M2.pin_1, M3.pin_1, hc-sr2.GND, hc-sr3.GND, hc-sr4.GND
  VCC: hc-sr1.VCC, hc-sr2.VCC, hc-sr3.VCC, hc-sr4.VCC, Q1.E, J1.vcc
  GND_2: hc-sr1.GND, VCC1.-, J1.gnd
  N13: Q1.C, VCC1.+

custom parts:
  MH-ET LIVE ESP32 DEVKIT 38 pins: http://mh.nodebb.com/topic/2/mh-et-live-esp32-devkit
