# Fritzing sketch Diagrama de conexion (saved by Fritzing 0.9.9b)

parts:
  Mod1 = Raspberry Pi 4B
  Cámara = Rasberry Pi NIOR Camera [chip_label=IC package="DIP (Dual Inline) [THT]"]  # not connected
  Servo = Basic Servo
  Motor_2 = DC Motor
  Motor_1 = DC Motor
  Pilas = Battery Holders [package=battery-aa]
  BAT2 = Battery Holders [package=battery-aa]
  BAT3 = Battery Holders [package=battery-aa]
  BAT4 = Battery Holders [package=battery-aa]
  L298N = H-Bridge with L298N
  LED_(traseros) = LED - 5mm [color="Red (633nm)" current=0.030 package="5 mm [THT]"]
  LEDs_(traseros) = LED - 5mm [color="Red (633nm)" current=0.030 package="5 mm [THT]"]
  LED3 = LED - 5mm [color="Orange (605nm)" current=0.030 package="5 mm [THT]"]
  LED4 = LED - 5mm [color="Orange (605nm)" current=0.030 package="5 mm [THT]"]
  LED5 = LED - 5mm [color="White (4500K)" current=0.030 package="5 mm [THT]"]
  LEDs_(delanteros) = LED - 5mm [color="White (4500K)" current=0.030 package="5 mm [THT]"]
  R1 = Resistor [tolerance=±5% resistance=1k power=0.25 package=THT]
  R2 = Resistor [tolerance=±5% resistance=1k power=0.25 package=THT]
  R3 = Resistor [tolerance=±5% resistance=1k power=0.25 package=THT]
  R4 = Resistor [tolerance=±5% resistance=1k power=0.25 package=THT]
  R5 = Resistor [tolerance=±5% resistance=1k power=0.25 package=THT]
  R6 = Resistor [tolerance=±5% resistance=1k power=0.25 package=THT]
  Reed_Switch = SWITCH-MOMENTARY-2 [package=reed_switch_pth]
  Giroscopio = MPU-6050 Board GY-521 [form="♀ (female)" package=THT]
  BMS = 2S-BMS
  Conversor_de_Nivel_Logico = TXB0108 8-channel Bi-directional Logic Level Converter
  Voltimetro = MH-DL18S [package=THT]
  Step_down = LM2596 step down module
  Interruptor = Toggle Switch [package=THT]
  IC1 = Rasberry Pi NIOR Camera [chip_label=IC package="DIP (Dual Inline) [THT]"]  # not connected
  LED7 = LED - 5mm [color="Orange (605nm)" current=0.030 package="5 mm [THT]"]
  LED8 = LED - 5mm [color="Orange (605nm)" current=0.030 package="5 mm [THT]"]
  R7 = Resistor [tolerance=±5% resistance=1k power=0.25 package=THT]
  R8 = Resistor [tolerance=±5% resistance=1k power=0.25 package=THT]
  Ultrasonido = HC-SR04 Ultrasonic Distance Sensor
  R9 = Resistor [tolerance=±5% power=0.25 resistance=1k package=THT]
  R10 = Resistor [tolerance=±5% power=0.25 resistance=10k package=THT]

nets:
  N1: Mod1.3V3, Giroscopio.pin1, Conversor_de_Nivel_Logico.OE, Conversor_de_Nivel_Logico.VCCA, R10.Pin_1
  5V: Mod1.5V, Servo.vcc, L298N.5V, R1.Pin_0, R2.Pin_0, R3.Pin_0, R4.Pin_0, R5.Pin_0, R6.Pin_0, Conversor_de_Nivel_Logico.VCCB, Ultrasonido.VCC
  N2: Mod1.GPIO2, Giroscopio.pin4
  N3: Mod1.GPIO3, Giroscopio.pin3
  GND: Mod1.GND, Servo.gnd, L298N.GND, LED_(traseros).cathode, LEDs_(traseros).cathode, LED3.cathode, LED4.cathode, LED5.cathode, LEDs_(delanteros).cathode, Reed_Switch.2, Giroscopio.pin2, Conversor_de_Nivel_Logico.GND, LED7.cathode, LED8.cathode, Ultrasonido.GND
  N4: Mod1.GPIO17, Ultrasonido.TRIG
  N5: Mod1.GPIO27, Conversor_de_Nivel_Logico.A2
  N6: Mod1.GPIO23, Conversor_de_Nivel_Logico.A1
  N7: Mod1.GPIO24, R9.Pin_1
  N8: Mod1.GPIO25, Servo.pulse
  N9: Mod1.GPIO6, L298N.ENA, L298N.ENB
  N10: Mod1.GPIO12, L298N.IN2, L298N.IN4
  N11: Mod1.GPIO13, L298N.IN1, L298N.IN3
  N12: Motor_2.pin_1, L298N.M2-01
  N13: Motor_2.pin_2, L298N.M2-02
  N14: Motor_1.pin_1, L298N.M1-02
  N15: Motor_1.pin_2, L298N.M1-01
  N16: Pilas.-, BAT4.-, Voltimetro.Battery_-
  N17: Pilas.+, BAT2.-, BAT3.-, BAT4.+, BMS.pin3#3
  N18: BAT2.+, BAT3.+, Interruptor.L2
  N19: Reed_Switch.1, R9.Pin_0, R10.Pin_0
  N20: BMS.pin1, Interruptor.COM
  N21: BMS.pin2, Voltimetro.Battery_+
  N22: BMS.pin3#2, Step_down.IN-, Step_down.OUT-
  N23: BMS.pin3#4, Step_down.IN+
  N24: Conversor_de_Nivel_Logico.B1, R7.Pin_0, R8.Pin_0
  N25: Conversor_de_Nivel_Logico.B2, Ultrasonido.ECHO

custom parts:
  Rasberry Pi NIOR Camera: Camera
  H-Bridge with L298N: h-bridge
  MPU-6050 Board GY-521: Acelerometro y Giroscopio MPU-6050 Board GY-521
  2S-BMS: 2S-BMS LIPO battery charger / protection unit. Note pcb does not match the board as it will likely connect with wires, so pcb is 5 pads suitable for .1in header pins.
  TXB0108 8-channel Bi-directional Logic Level Converter: Because the Arduino (and Basic Stamp) are 5V devices, and most modern sensors, displays, flash cards and modes are 3.3V-only, many makers find that they need to perform level shifting/conversion to protect the 3.3V device from 5V. Although one can use resistors to make a divider, for high speed transfers, the resistors can add a lot of slew and cause havoc that is tough to debug. For that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
  MH-DL18S: 1S 2S 3S 4S Single 3.7V Lithium battery capacity LED indicator module.
  LM2596 step down module: LM2596 DC-DC step down power supply module 3 A.
